# Fritzing sketch digispark_IR_LED_Photodiode (saved by Fritzing 0.8.0b)
breadboards: 1

parts:
  R10 = Resistor [tolerance=±5% resistance=10k package=THT]
  IC2 = IC, DIP package, 8 pins [chip_label=ATtiny85]
  CONN2 = USB connector [package=THT]
  R13 = Resistor [tolerance=±5% resistance=68 part_number="68 ohm" package=THT]
  R14 = Resistor [tolerance=±5% resistance=68 package=THT]
  R15 = Resistor [tolerance=±5% resistance=1.5k package=THT]
  D3 = Rectifier Diode
  D4 = Rectifier Diode
  LED14 = LED - 5mm [color="Red (633nm)" package="5 mm [THT]"]
  R16 = Resistor [tolerance=±5% resistance=150 package=THT]
  LED15 = LED - 5mm [color="Infrared (850nm)" package="5 mm [THT]"]
  LED16 = LED - 5mm [color="Infrared (940nm)" package="5 mm [THT]"]

nets:
  N1: R10.Pin_0, IC2.pin7, LED14.anode, LED16.anode
  N2: IC2.pin2, R13.Pin_0
  N3: IC2.pin4, CONN2.GND, CONN2.chassis5, CONN2.chassis6, D3.anode, D4.anode, LED14.cathode, LED15.cathode
  N4: IC2.pin8, CONN2.5V, R15.Pin_1, R16.Pin_0, LED16.cathode
  N5: CONN2.d-, R13.Pin_1, R15.Pin_0, D4.cathode
  N6: CONN2.d+, R14.Pin_1, D3.cathode
  N7: R16.Pin_1, LED15.anode

notes:
  IR LED (white) as transmitter and Photodiode (black)as receiver is used.
  Both the led's should be kept as near as possible for better reception.
  Connecting PB2/Pin7 of Digispark with anode of photodiode.Cover the photodiode with black tape etc to restrict ambient light.
  Red wire:VCC
  Black wire:GND

custom parts:
  Rectifier Diode: Ageneral purpose zener diode
