# Fritzing sketch digispark_LM35_temperaturesensor (saved by Fritzing 0.8.0b)
breadboards: 1

parts:
  IC2 = IC, DIP package, 8 pins [chip_label=ATtiny85]
  CONN2 = USB connector [package=THT]
  R4 = Resistor [tolerance=±5% resistance=68 part_number="68 ohm" package=THT]
  R5 = Resistor [tolerance=±5% resistance=68 package=THT]
  R6 = Resistor [tolerance=±5% resistance=1.5k package=THT]
  D3 = Rectifier Diode
  D4 = Rectifier Diode
  T1 = LM35 Temperature Sensor [package="TO92 [THT]"]

nets:
  N1: IC2.pin2, R4.Pin_0
  N2: IC2.pin3, R5.Pin_0
  GND: IC2.pin4, CONN2.GND, CONN2.chassis5, CONN2.chassis6, D3.anode, D4.anode, T1.GND
  N3: IC2.pin7, T1.Vout
  N4: IC2.pin8, CONN2.5V, R6.Pin_1, T1.+Vs
  N5: CONN2.d-, R4.Pin_1, R6.Pin_0, D4.cathode
  N6: CONN2.d+, R5.Pin_1, D3.cathode

notes:
  USB-->ATtiny85-20pu
  D- -->Pin2--PB3
  D+ -->Pin3--PB4
  Vcc -->Pin8
  GND -->Pin4
  3.6V zener diode
  Caution:Anode should be ground

custom parts:
  Rectifier Diode: Ageneral purpose zener diode
