# Fritzing sketch digispark_breadboard (saved by Fritzing 0.8.0b)
breadboards: 1

parts:
  IC1 = IC, DIP package, 8 pins [chip_label=ATtiny85]
  CONN1 = USB connector [package=THT]
  R1 = Resistor [tolerance=±5% resistance=1.5k package=THT]
  D1 = Rectifier Diode
  D2 = Rectifier Diode
  R3 = Resistor [tolerance=±5% resistance=68 package=THT]
  R2 = Resistor [tolerance=±5% resistance=68 part_number="68 ohm" package=THT]

nets:
  N1: IC1.pin2, R2.Pin_0
  N2: IC1.pin3, R3.Pin_0
  N3: IC1.pin4, CONN1.GND, CONN1.chassis5, CONN1.chassis6, D1.anode, D2.anode
  N4: IC1.pin8, CONN1.5V, R1.Pin_1
  N5: CONN1.d-, R1.Pin_0, D1.cathode, R2.Pin_1
  N6: CONN1.d+, D2.cathode, R3.Pin_1

notes:
  usb connections with ATtiny 85
  D- -->Pin2--PB3
  D+ -->Pin3--PB4
  Vcc -->Pin8
  GND -->Pin4

custom parts:
  Rectifier Diode: Ageneral purpose zener diode
