# Fritzing sketch ArduinoISP_attiny85.png (saved by Fritzing 0.8.0b)
breadboards: 1

parts:
  Arduino_UNO = Arduino
  C1 = Electrolytic Capacitor [capacitance=1µF package="100 mil [THT, electrolytic]"]
  attiny = IC, DIP package, 8 pins [chip_label=IC]

nets:
  N1: Arduino_UNO.GND, C1.-, attiny.pin4
  N2: Arduino_UNO.D13, attiny.pin7
  N3: Arduino_UNO.D12, attiny.pin6
  N4: Arduino_UNO.D11, attiny.pin5
  N5: Arduino_UNO.D10, attiny.pin1
  N6: Arduino_UNO.RST, C1.+
  N7: Arduino_UNO.+5V, attiny.pin8
